# Fritzing sketch Arduino VFD (saved by Fritzing 0.9.3b)

parts:
  J1 = male pin header, 4 pins [form="♂ (male)"]
  Part1 = Arduino Nano (Rev3.0)
  X1 = DB9 Connector [package=db9]
  JACK1 = 2.1mm Barrel Jack with Terminal Block
  J2 = male pin header, 3 pins [form="♂ (male)"]

nets:
  N1: J1.pin1, Part1.5V
  N2: J1.pin3, Part1.D9
  N3: J1.pin4, Part1.GND
  N4: X1.5, JACK1.NEG, J2.pin2
  N5: X1.8, J2.pin3
  N6: JACK1.POS, J2.pin1

notes:
  12V DC
  TTL RS232 Convertor
  RS232 Pinout is Ground on Pin 5, Rx on Pin 2)
  VFD Display
  MAX232 chip converts serial signals from TTL (0 - 5V) to RS232 (+15V - -15V)
  AltSoftSerial library uses Pin 9 for transmit (Pin 8 is receive, but not required in this case, since we are only sending data *to* to the display)
